# Fritzing sketch StepperControllerV2 (saved by Fritzing 0.9.3b)
circuit board: 11.1148cm x 9.81735cm
breadboards: 1

parts:
  C1 = Capacitor Polarized [package=cpol-radial-100uf-25v]
  DRV_3 = DRV 8825 Stepper Motor Carrier, High Current [part_number="DRV 8825"]
  JP1 = female pin header, 12 pins [form="♀ (female)"]
  Part3 = Arduino Nano (Rev3.0)
  Sensor = molex pin header, 2 pins [form=molex]
  12v = molex pin header, 2 pins [form=molex]
  Speaker = female pin header, 1 pin [form="♀ (female)"]
  J3 = female pin header, 1 pin [form="♀ (female)"]
  Motor = molex pin header, 4 pins [form=molex]
  Aux = molex pin header, 4 pins [form=molex]
  LED = molex pin header, 3 pins [form=molex]
  Reset = molex pin header, 2 pins [form=molex]
  JP3 = rounded female pin header, 2 pins [form="♀ (female rounded)"]
  Pad3 = Pad [width=3.175 height=2.187222222222222 connect=center]
  C2 = Capacitor Polarized [package=cpol-radial-100uf-25v]
  R1 = Resistor [tolerance=±5% resistance=100 package=THT]
  D1 = Rectifier Diode [part_number=1N4001 package="300 mil [THT]"]
  JP4 = rounded female pin header, 2 pins [form="♀ (female rounded)"]

nets:
  N1: C1.+, DRV_3.VOLTAGE_ST/_MT, Part3.VIN, 12v.pin1
  N2: C1.-, DRV_3.GROUND_ST/_MT, DRV_3.GROUND_LOG, JP1.pin1, Part3.GND, 12v.pin2, Speaker.pin1, Aux.pin1, LED.pin2, Reset.pin1, JP3.pin1, C2.-
  N3: DRV_3.MS1, DRV_3.MS2, DRV_3.MS3, DRV_3.RESET, DRV_3.SLEEP, Part3.5V, Aux.pin2, LED.pin3, C2.+, R1.Pin_1
  N4: DRV_3.STEP, Part3.A3
  N5: DRV_3.DIRECTION, Part3.A2
  N6: DRV_3.OUT_2B, Motor.pin1
  N7: DRV_3.OUT_2A, Motor.pin2
  N8: DRV_3.OUT_1A, Motor.pin3
  N9: DRV_3.OUT_1B, Motor.pin4
  N10: JP1.pin2, Part3.D2, R1.Pin_0, D1.anode, JP4.pin1
  N11: JP1.pin3, Part3.D3, LED.pin1
  N12: JP1.pin4, Part3.D4
  N13: JP1.pin5, Part3.D5
  N14: JP1.pin6, Part3.D6
  N15: JP1.pin7, Part3.D7
  N16: JP1.pin8, Part3.D8
  N17: JP1.pin9, Part3.D9
  N18: JP1.pin10, Part3.D10
  N19: JP1.pin11, Part3.D11/MOSI
  N20: JP1.pin12, Part3.D12/MISO
  N21: Part3.RESET, Reset.pin2
  N22: Part3.A6, J3.pin1
  N23: Part3.A1, Aux.pin4
  N24: Part3.A0, Aux.pin3
  N25: Sensor.pin2, D1.cathode, JP4.pin2
  N26: JP3.pin2, Pad3.pad

notes:
  github.com/jburgess/buzzzmas
  -
  +
  v2
